# Fritzing sketch Diagrama de conexion Arduino (saved by Fritzing 0.9.3b)
perfboards: 1

parts:
  Espessif_Serial_Wifi_Modul_1 = ESP8266 ESP01 [part_number=ESP8266 package=THT]
  S1 = H-Bridge with L298N
  R-Motor = DC Motor with two-phase hall-encoder [part_number=VT-E-G25A-06-177E]
  S2 = Pololu QTR-8 Reflectabce Sensor array [package=THT]
  Componente1 = Arduino Uno (Rev3)
  L-Motor = DC Motor with two-phase hall-encoder [part_number=VT-E-G25A-06-177E]

nets:
  GND: Espessif_Serial_Wifi_Modul_1.GND, S1.GND, R-Motor.pin5, S2.pin15, Componente1.GND, L-Motor.pin5
  N1: Espessif_Serial_Wifi_Modul_1.RXD, Componente1.D12/MISO
  N2: Espessif_Serial_Wifi_Modul_1.TXD, Componente1.D13/SCK
  VCC: Espessif_Serial_Wifi_Modul_1.VCC, Espessif_Serial_Wifi_Modul_1.GPIO02, Espessif_Serial_Wifi_Modul_1.CH_PD, Componente1.3V3
  N3: S1.12V, R-Motor.pin6
  N4: S1.IN1, Componente1.D8
  N5: S1.IN2, Componente1.D9_PWM
  N6: S1.IN3, Componente1.D11_PWM/MOSI
  N7: S1.IN4, Componente1.D10_PWM/SS
  N8: S1.OUT3-Motor2, R-Motor.pin2
  N9: S1.OUT4-Motor2, R-Motor.pin1
  N10: S1.OUT1-Motor1, L-Motor.pin1
  N11: S1.OUT2-Motor1, L-Motor.pin2
  N12: R-Motor.pin3, Componente1.D7
  N13: R-Motor.pin4, Componente1.D6_PWM
  N14: S2.pin7, Componente1.A0
  N15: S2.pin8, Componente1.A1
  N16: S2.pin9, Componente1.A2
  N17: S2.pin10, Componente1.A3
  N18: S2.pin11, Componente1.A4/SDA
  N19: S2.pin12, Componente1.A5/SCL
  N20: S2.pin13, Componente1.D3_PWM
  N21: S2.pin14, Componente1.5V, L-Motor.pin6
  N22: Componente1.D4, L-Motor.pin3
  N23: Componente1.D5_PWM, L-Motor.pin4

notes:
  PINOUT Arduino UNO
  Pines Digitales
  0 -
  1 -
  2 -
  3 - LED Sensores(Gris)
  4 - Encoder A Motor R(Blanco)
  5 - Encoder B Motor R(Blanco)
  6 - Encoder B Motor L(Morado)
  7 - Encoder A Motor L(Morado)
  8 - IN1 Motores(Naranja)
  9 - IN2 Motores(Verde)
  10 - IN 4 Motores(Morado)
  11 - IN 3 Motores(Azul)
  12 - RX WiFi(Blanco)
  13 - TX WiFi(Gris)
  Pines Analogos
  A0 - Sensor 6(Blanco)
  A1 - Sensor 5(Naranja)
  A2 - Sensor 4(Morado)
  A3 - Sensor 3(Ocre)
  A4 - Sensor 2(Negro)
  A5 - Sensor 1(Ocre)
  Componentes
  Arduino UNO
  Tarjeta Driver L298N
  Modulo WiFi ESP01S
  2 Motores DC
  2 Encoders SEN0116
  Tarjeta de sensores QTR-8RC
  Baquelita
  Motor DC
  1 - Motor +
  2 - Encoder +
  3 - Encoder Phase A
  4 - Encoder Phase B
  5 - Encoder -
  6 - Motor -

custom parts:
  ESP8266 ESP01: Generic WiFi Module based on the ESP8266 with onboard PCB antenna and UART communications
  H-Bridge with L298N: h-bridge
