# Fritzing sketch Diagrama de conexion Arduino (saved by Fritzing 0.9.3b)

parts:
  Espessif_Serial_Wifi_Modul_1 = ESP8266 ESP01 [part_number=ESP8266 package=THT]
  Componente1 = Arduino Uno (Rev3)
  S1 = H-Bridge with L298N
  VCC1 = Battery block 9V
  DC_Mot_Enc1 = DC Motor with two-phase hall-encoder [part_number=VT-E-G25A-06-177E]
  DC_Mot_Enc2 = DC Motor with two-phase hall-encoder [part_number=VT-E-G25A-06-177E]
  S2 = Pololu QTR-8 Reflectabce Sensor array [package=THT]
  IC1 = Voltage Regulator [package=to-92]
  Componente2 = JeePlug experimenter's board

nets:
  GND: Espessif_Serial_Wifi_Modul_1.GND, Componente1.A2, Componente1.A3, Componente1.A4/SDA, Componente1.A5/SCL, Componente1.GND, S1.GND, VCC1.-, DC_Mot_Enc1.pin5, DC_Mot_Enc2.pin5, S2.pin1, S2.pin7, S2.pin8, S2.pin9, S2.pin10, S2.pin15, S2.pin18, S2.pin19, S2.pin20, S2.pin21, IC1.IN, Componente2.N$31, Componente2.N$32, Componente2.N$33, Componente2.N$34, Componente2.N$35, Componente2.N$37
  N1: Espessif_Serial_Wifi_Modul_1.RXD, Componente1.D2
  N2: Espessif_Serial_Wifi_Modul_1.TXD, Componente1.D3_PWM
  VCC: Espessif_Serial_Wifi_Modul_1.VCC, Espessif_Serial_Wifi_Modul_1.CH_PD, Componente1.3V3, Componente2.B3, Componente2.B2, Componente2.B1
  N3: Componente1.A0, Componente1.D4, S2.pin12, S2.pin13, S2.pin23
  N4: Componente1.A1, S1.5V, DC_Mot_Enc1.pin2, DC_Mot_Enc2.pin2, S2.pin2, S2.pin11, S2.pin14, S2.pin22, IC1.OUT, Componente2.N$39, Componente2.N$41, Componente2.N$46
  N5: Componente1.D8, DC_Mot_Enc2.pin4
  N6: Componente1.D9_PWM, S2.pin3
  N7: Componente1.D10_PWM/SS, S1.IN3
  N8: Componente1.D11_PWM/MOSI, S1.IN4
  N9: Componente1.D12/MISO, DC_Mot_Enc1.pin3
  N10: Componente1.D13/SCK, DC_Mot_Enc1.pin4
  N11: Componente1.D5_PWM, S1.IN1
  N12: Componente1.D6_PWM, S1.IN2
  N13: Componente1.D7, DC_Mot_Enc2.pin3
  VIN: Componente1.VIN, S1.12V, VCC1.+, IC1.GND, Componente2.N$23, Componente2.N$25, Componente2.N$30, Componente2.N$64
  N14: S1.OUT3-Motor2, DC_Mot_Enc1.pin6
  N15: S1.OUT4-Motor2, DC_Mot_Enc1.pin1
  N16: S1.OUT1-Motor1, DC_Mot_Enc2.pin1
  N17: S1.OUT2-Motor1, DC_Mot_Enc2.pin6

notes:
  Motor DC
  1 - Motor +
  2 - Encoder +
  3 - Encoder Phase A
  4 - Encoder Phase B
  5 - Encoder -
  6 - Motor -
  PINOUT Arduino UNO
  Pines Digitales
  0 -
  1 -
  2 - RX WiFi(Amarillo)
  3 - TX WiFi(Amarillo)
  4 - LED Sensores(Café)
  5 - IN1 Motores(Azul)
  6 - IN 2 Motores(Azul)
  7 - Encoder A Motor 1(Morado)
  8 - Encoder B Motor 1(Morado)
  9 - Sensor 8(Ocre)
  10 - IN 3 Motores(Gris)
  11 - IN 4 Motores(Gris)
  12 - Encoder A Motor 2(Blanco)
  13 - Encoder B Motor 2(Blanco)
  Pines Analogos
  A0 - Sensor 1(Ocre)
  A1 - Sensor 2(Ocre)
  A2 - Sensor 3(Ocre)
  A3 - Sensor 4(Ocre)
  A4 - Sensor 5(Ocre)
  A5 - Sensor 6(Ocre)
  Componentes
  Arduino UNO
  Tarjeta Driver L298N
  Modulo WiFi ESP01S
  2 Motores DC
  2 Encoders SEN0116
  Tarjeta de sensores QTR-8RC
  Regulador de Voltaje 7805
  PCB universal
  Bateria 9V
  Regla de Colores Voltajes
  Verde 3.3V
  Naranja 5V
  Rojo 9V
  Negro GND

custom parts:
  ESP8266 ESP01: Generic WiFi Module based on the ESP8266 with onboard PCB antenna and UART communications
  H-Bridge with L298N: h-bridge
